// Logisim project x69pp.circ as structural Verilog: 19 circuits, main circuit main
module main (
);

  wire aludecoder_1_ien, and_1_out, and_2_out, and_3_out, bitfinder_1_found, buslock_1_out_3, button_1_out,
       clock_1_out, decoder_1_out0, decoder_1_out1, decoder_1_out2, decoder_1_out3, dipswitch_1_sw8,
       memorybusadapter_i_1_out_2, memorybusadapter_i_1_out_3, monostable_1_out_2, monostable_2_out_2,
       pull_resistor_5_node, rgbled_1_p1, rgbled_1_p2, rgbled_1_p3, transistor_1_out, transistor_3_out;
  wire [1:0] adder_1_out, bitfinder_1_index;
  wire [2:0] bit_extender_2_out;
  wire [3:0] aludecoder_1_ra, aludecoder_1_rb, aludecoder_1_rd, cpucore_1_rao, cpucore_1_rao_2,
       cpucore_1_rao_3, cpucore_1_rao_4, cpucore_1_rbo, cpucore_1_rbo_2, cpucore_1_rbo_3, cpucore_1_rbo_4;
  wire [4:0] aludecoder_1_op;
  wire [7:0] counter_1_q;
  wire [15:0] aludecoder_1_ime, bit_extender_1_out, memorybusadapter_i_1_out_4, memorybusadapter_i_1_out_5,
       ram_1_dout;
  wire [31:0] rom_1_data;
  wire [33:0] controlled_buffer_1_out, memorybusadapater_o_1_out_5;

  Button button_1 (.out(button_1_out));
  Transistor #(.gate("br"), .\type ("n")) transistor_1 (.in(1'b0), .out(transistor_1_out), .gate(clock_1_out));
  Clock clock_1 (.out(clock_1_out));
  Monostable monostable_1 (.out_2(monostable_1_out_2), .in_1(rgbled_1_p1));
  // RGBLED rgbled_1: pin names not known; wires that end beside it: rgbled_1_p1, rgbled_1_p2, rgbled_1_p3, rgbled_1_p1
  Pull_Resistor pull_resistor_1 (.node(rgbled_1_p3));
  T_Flip_Flop t_ff_1 (.clk(button_1_out), .T(1'b1), .Q(rgbled_1_p3));  // open: Qn, preset, reset
  Pull_Resistor #(.pull(1)) pull_resistor_2 (.node(transistor_1_out));
  Monostable monostable_2 (.out_2(monostable_2_out_2), .in_1(transistor_1_out));
  ROM #(.dataWidth(32)) rom_1 (.addr(counter_1_q), .data(rom_1_data));
  Counter #(.max('h20), .trigger("falling")) counter_1 (
    .Q(counter_1_q), .clk(and_3_out), .clr(monostable_1_out_2));  // open: load, D, count, carry, up
  Pull_Resistor #(.pull(1)) pull_resistor_3 (.node(rgbled_1_p2));
  Transistor #(.gate("br"), .\type ("n")) transistor_2 (.in(1'b0), .out(rgbled_1_p2), .gate(rgbled_1_p1));
  Pull_Resistor pull_resistor_4 (.node(rgbled_1_p1));
  and and_1 (and_1_out, rgbled_1_p3, monostable_2_out_2);
  RSLatch rslatch_1 (.out_3(rgbled_1_p1), .in_1(and_1_out), .in_2(and_2_out));  // open: out_4
  and and_2 (and_2_out, monostable_2_out_2, ~rgbled_1_p3);  // AND_Gate
  and and_3 (and_3_out, rgbled_1_p1, clock_1_out);
  Pull_Resistor #(.pull(1)) pull_resistor_5 (.node(pull_resistor_5_node));
  DipSwitch dipswitch_1 (.sw8(dipswitch_1_sw8));  // open: sw1, sw2, sw3, sw4, sw5, sw6, sw7
  Hex_Digit_Display hex_digit_display_1 (.value(cpucore_1_rbo_4));  // open: dp
  Hex_Digit_Display hex_digit_display_2 (.value(cpucore_1_rao_4));  // open: dp
  assign bit_extender_1_out = {{8{1'b0}}, counter_1_q};  // Bit_Extender bit_extender_1
  Hex_Digit_Display hex_digit_display_3 (.value(bit_extender_1_out[15:12]));  // open: dp
  Bit_Extender #(.in_width(32), .out_width(3), .\type ("zero")) bit_extender_2 (
    .in(rom_1_data), .out(bit_extender_2_out));
  Hex_Digit_Display hex_digit_display_4 (.value(cpucore_1_rbo_3));  // open: dp
  Hex_Digit_Display hex_digit_display_5 (.value(cpucore_1_rbo_2));  // open: dp
  Hex_Digit_Display hex_digit_display_6 (.value(cpucore_1_rao_3));  // open: dp
  Hex_Digit_Display hex_digit_display_7 (.value(cpucore_1_rao_2));  // open: dp
  Hex_Digit_Display hex_digit_display_8 (.value(bit_extender_1_out[11:8]));  // open: dp
  Hex_Digit_Display hex_digit_display_9 (.value(bit_extender_1_out[7:4]));  // open: dp
  BitFinder #(.width(3)) bitfinder_1 (.in(bit_extender_2_out), .index(bitfinder_1_index), .found(bitfinder_1_found));
  ALUDecoder aludecoder_1 (
    .rD(aludecoder_1_rd), .IME(aludecoder_1_ime), .iEN(aludecoder_1_ien), .OP(aludecoder_1_op),
    .rA(aludecoder_1_ra), .rB(aludecoder_1_rb), .in_1(rom_1_data));  // open: bEN, FLG
  MemoryBusAdapter_I memorybusadapter_i_1 (
    .out_2(memorybusadapter_i_1_out_2), .out_3(memorybusadapter_i_1_out_3),
    .out_4(memorybusadapter_i_1_out_4), .out_5(memorybusadapter_i_1_out_5), .in_1(controlled_buffer_1_out));
  Hex_Digit_Display hex_digit_display_10 (.value(cpucore_1_rbo));  // open: dp
  Hex_Digit_Display hex_digit_display_11 (.value(cpucore_1_rao));  // open: dp
  Hex_Digit_Display hex_digit_display_12 (.value(bit_extender_1_out[3:0]));  // open: dp
  Adder #(.width(2)) adder_1 (
    .a(bitfinder_1_index), .b(2'b00), .out(adder_1_out), .cin(bitfinder_1_found));  // open: cout
  Decoder #(.enable("false"), .select(2)) decoder_1 (
    .out0(decoder_1_out0), .out1(decoder_1_out1), .out2(decoder_1_out2), .out3(decoder_1_out3),
    .sel(adder_1_out));
  assign controlled_buffer_1_out = buslock_1_out_3 ? memorybusadapater_o_1_out_5 : 34'bz;  // Controlled_Buffer controlled_buffer_1
  MemoryBusAdapater_O memorybusadapater_o_1 (
    .out_5(memorybusadapater_o_1_out_5), .in_4(ram_1_dout));  // open: in_1, in_2, in_3
  RAM #(.addrWidth(16), .dataWidth(16)) ram_1 (
    .addr(memorybusadapter_i_1_out_4), .we(memorybusadapter_i_1_out_3), .oe(transistor_3_out),
    .clk(memorybusadapter_i_1_out_2), .din(memorybusadapter_i_1_out_5), .dout(ram_1_dout));
  Transistor #(.\type ("n")) transistor_3 (.in(1'b0), .out(transistor_3_out), .gate(memorybusadapter_i_1_out_3));
  Pull_Resistor #(.pull(1)) pull_resistor_6 (.node(transistor_3_out));
  BusLock buslock_1 (.out_3(buslock_1_out_3), .in_2(pull_resistor_5_node), .in_1(dipswitch_1_sw8));
  CPUCore cpucore_1 (
    .rAO({cpucore_1_rao_4, cpucore_1_rao_3, cpucore_1_rao_2, cpucore_1_rao}),
    .rBO({cpucore_1_rbo_4, cpucore_1_rbo_3, cpucore_1_rbo_2, cpucore_1_rbo}), .ALUen(decoder_1_out1),
    .DIn(aludecoder_1_ime), .rD(aludecoder_1_rd), .IMEen(aludecoder_1_ien), .rA(aludecoder_1_ra),
    .rB(aludecoder_1_rb), .ALUop(aludecoder_1_op), .CLK(and_3_out));
  Transistor #(.\type ("n")) transistor_4 (.in(1'b0), .out(pull_resistor_5_node), .gate(buslock_1_out_3));

  // Notes on the sheet:
  //   ON / OFF
  //   contents of rom_1 (hex, n*v repeats v):
  //   1 39 11101 11139 129 10129 129 10129 129 10129 129 10129 129 10129 129 10129 129 10129 129 10129 129
  //   10129 129 10129 129 10129 129 10129 129 10129 129 10129 8a0c79ed 12de2a36 a2a9e37e 4491dbb 758461e6
  //   1895675 90e64c6b d8224705 2c2a0ed2 7756363 e5890fc4 e1bba157 5153ea43 c08bd095 47fcb665 a071d785
  //   19421db5 10427d03 352291e9 f6269499 c79cc0ce f99671fe f8625e94 348b49e6 78b027e7 55f3e961 d1f79f73
  //   1609c25d ba4116ca 51dc0306 c97618c1 f252171e 462adbbd 4e2bdd7c 57310c8c befad952 939596bf 22f005f6
  //   9bc71d98 46198537 7bb33111 afea7385 f4cefc83 6c86927b 30d5c8f7 86a08189 6ebf4329 f8e1b5ce 9a9a95bf
  //   5d299d65 90ee2249 70a027b2 6c108802 e74e9b71 df2bc568 cab80495 19722a29 e814e734 e74490f5 b5191a20
  //   167e8532 77d002d2 e5e69ead 5c54b5d1 64f50db4 fd8709c3 c0381c41 40db48c7 a074dd20 8d232ac5 e4227035
  //   f44ff4dc 123fbb49 c9b74d13 6330490a 38df56f8 6065bc25 138054d7 791afa9f 1d8822a4 98e675d4 5f40badc
  //   7a05cdd3 5a1962dd 66a112e2 3f916b87 932c266f 7593742a 6bbcc4c9 43ed2107 b5b1a343 96d60bf0 fc75ab9
  //   2bdaaccb ac919c8e 4356e105 8f60009a 89ede434 a69da4a2 9741c982 14206a51 499e248c 2a50eec8 971c61dc
  //   ddd6ef42 476ca235 6538c060 5a149135 a6485a15 6bc3f725 6210504c c6c27eef fed870bd d19da491 d9b0b88f
  //   179bcd82 4fe478b6 b9917be8 e1dbde30 11df2e8f bc8b3b8d dbbe2302 abf37364 d69ca435 9f524fa5 6392799
  //   331b77eb 1af003a2 c4d0a937 7da855f7 2759dbba d7c88ceb 6582b79a e18d46f1 783b27d9 abf1ac20 176c92c4
  //   30e75913 a79e518e 19be379b 3772fd10 355f891c f2c81bbb edf8bf98 599c3d41 674ddac 7700aa84 bcd0c30a
  //   22f614c6 6a575a3b b6042d34 d4a5ddac 7ee563f b28aad4d 5fb9c261 fb0f4355 abfe03f de490de3 8831fa4d
  //   ff8f1c90 76e0053 8f31fc34 95209b8e be46986b e9e48243 ed57d99d 3b1b8df1 bcf8c78f 6772ef97 617a8bd5
  //   3230f9c 9af79491 533dc35c ee6c9f64 92959872 2a776d86 3da89627 80839d55 84f40fba 1c7b72dc dd68865a
  //   4acb882a 26013802 a9553f67 661e60a5 f8c0b40f fe117541 dbd09dba d04c4ccf 47d26e53 880e513b fdd4beb8
  //   997302b6 69242813 d3036229 cfc9c56a 555ecb94 312a1837 66407798 79aabc11 bb6cd383 a31988a2 c9773191
  //   a299467f a0158f42 50f442a4 3ff865f9 8349a5a2 7c913a39 8979ceb3 e997f83b 9df2e061 37b0ba 8ac07b5b
  //   cb040723 a4d825aa 698d2a89 45e35f72 94c6950d ec3dbbcb 9401999e 7d51cb8f 19f70e3e eed1101
  //   LOCK
  //   B
  //   A
  //   PC
endmodule

module MonostableCD (
  input  in_1,
  input  in_2,
  output out_3,
  output out_4
);

  wire buffer_1_out, pull_resistor_2_node, pull_resistor_3_node, transistor_2_out;

  buf buffer_1 (buffer_1_out, in_2);
  Pull_Resistor pull_resistor_1 (.node(buffer_1_out));
  Pull_Resistor #(.pull(1)) pull_resistor_2 (.node(pull_resistor_2_node));
  Transistor #(.\type ("n")) transistor_1 (.in(1'b0), .out(pull_resistor_2_node), .gate(in_1));
  Transistor #(.gate("br"), .\type ("n")) transistor_2 (.in(1'b0), .out(transistor_2_out), .gate(buffer_1_out));
  Pull_Resistor #(.pull(1)) pull_resistor_3 (.node(pull_resistor_3_node));
  Transistor #(.gate("br"), .\type ("n")) transistor_3 (
    .in(pull_resistor_2_node), .out(pull_resistor_3_node), .gate(transistor_2_out));
  Pull_Resistor #(.pull(1)) pull_resistor_4 (.node(transistor_2_out));
  Pull_Resistor pull_resistor_5 (.node(out_4));
  Transistor transistor_4 (.in(1'b1), .out(out_4), .gate(pull_resistor_3_node));

  assign out_3 = in_2;

  // Notes on the sheet:
  //   in_2: pull=down
  //   out_3: pull=down
  //   in_1: pull=down
endmodule

module Monostable (
  input  in_1,
  output out_2
);

  wire buffer_1_out, pull_resistor_3_node, transistor_1_out, transistor_3_out;

  Transistor #(.\type ("n")) transistor_1 (.in(1'b0), .out(transistor_1_out), .gate(in_1));
  buf buffer_1 (buffer_1_out, in_1);
  Pull_Resistor pull_resistor_1 (.node(buffer_1_out));
  Pull_Resistor #(.pull(1)) pull_resistor_2 (.node(transistor_1_out));
  Pull_Resistor #(.pull(1)) pull_resistor_3 (.node(pull_resistor_3_node));
  Transistor #(.gate("br"), .\type ("n")) transistor_2 (
    .in(transistor_1_out), .out(pull_resistor_3_node), .gate(transistor_3_out));
  Transistor #(.gate("br"), .\type ("n")) transistor_3 (.in(1'b0), .out(transistor_3_out), .gate(buffer_1_out));
  Pull_Resistor #(.pull(1)) pull_resistor_4 (.node(transistor_3_out));
  Pull_Resistor pull_resistor_5 (.node(out_2));
  Transistor transistor_4 (.in(1'b1), .out(out_2), .gate(pull_resistor_3_node));
endmodule

module RSLatch (
  input  in_1,
  input  in_2,
  output out_3,
  output out_4
);

  S_R_Flip_Flop s_r_ff_1 (.Q(out_3), .Qn(out_4), .preset(in_1), .reset(in_2));  // open: S, clk, R
endmodule

module BusLock (
  input  in_1,
  input  in_2,
  output out_3
);

  wire and_1_out, monostable_1_out_2, transistor_1_out;

  Transistor #(.\type ("n")) transistor_1 (.in(1'b0), .out(transistor_1_out), .gate(in_1));
  Monostable monostable_1 (.out_2(monostable_1_out_2), .in_1(transistor_1_out));
  Pull_Resistor #(.pull(1)) pull_resistor_1 (.node(transistor_1_out));
  and and_1 (and_1_out, in_1, in_2);
  Pull_Resistor pull_resistor_2 (.node(out_3));
  RSLatch rslatch_1 (.out_3(out_3), .in_1(and_1_out), .in_2(monostable_1_out_2));  // open: out_4

  // Notes on the sheet:
  //   in_1: pull=down
endmodule

module TSRS (
  input  in_1,
  input  in_2,
  output out_3,
  output out_4
);

  wire dipswitch_1_sw7, dipswitch_1_sw8, pull_resistor_2_node;

  DipSwitch dipswitch_1 (.sw7(dipswitch_1_sw7), .sw8(dipswitch_1_sw8));  // open: sw1, sw2, sw3, sw4, sw5, sw6
  Pull_Resistor #(.pull(1)) pull_resistor_1 (.node(out_3));
  Transistor #(.\type ("n")) transistor_1 (.in(1'b0), .out(out_3), .gate(in_1));
  Transistor #(.\type ("n")) transistor_2 (.in(1'b0), .out(out_3), .gate(out_4));
  Pull_Resistor pull_resistor_2 (.node(pull_resistor_2_node));
  Transistor transistor_3 (.in(pull_resistor_2_node), .out(out_4), .gate(out_3));
  Transistor transistor_4 (.in(1'b1), .out(pull_resistor_2_node), .gate(in_2));
  Pull_Resistor pull_resistor_3 (.node(out_4));
endmodule

module MemoryBusAdapter_I (
  input  [33:0] in_1,
  output out_2,
  output out_3,
  output [15:0] out_4,
  output [15:0] out_5
);


  assign out_2 = in_1[33];
  assign out_3 = in_1[32];
  assign out_4 = in_1[31:16];
  assign out_5 = in_1[15:0];
endmodule

module MemoryBusAdapater_O (
  input  in_1,
  input  in_2,
  input  [15:0] in_3,
  input  [15:0] in_4,
  output [33:0] out_5
);


  assign out_5 = {in_1, in_2, in_3, in_4};
endmodule

module CPURegs16 (
  input  in_1,
  input  CLR,
  input  [15:0] in_3,
  input  [3:0] in_4,
  input  [3:0] in_5,
  input  [3:0] in_6,
  output [15:0] out_7,
  output [15:0] out_8
);

  wire demultiplexer_1_out0, demultiplexer_1_out1, demultiplexer_1_out2, demultiplexer_1_out3,
       demultiplexer_1_out4, demultiplexer_1_out5, demultiplexer_1_out6, demultiplexer_1_out7,
       demultiplexer_1_out8, demultiplexer_1_out9, demultiplexer_1_out10, demultiplexer_1_out11,
       demultiplexer_1_out12, demultiplexer_1_out13, demultiplexer_1_out14, demultiplexer_1_out15;
  wire [15:0] reg16_1_out_4, reg16_2_out_4, reg16_3_out_4, reg16_4_out_4, reg16_5_out_4, reg16_6_out_4,
       reg16_7_out_4, reg16_8_out_4, reg16_9_out_4, reg16_10_out_4, reg16_11_out_4, reg16_12_out_4,
       reg16_13_out_4, reg16_14_out_4, reg16_15_out_4, reg16_16_out_4;

  Demultiplexer #(.enable("false"), .select(4)) demultiplexer_1 (
    .out0(demultiplexer_1_out0), .out1(demultiplexer_1_out1), .out2(demultiplexer_1_out2),
    .out3(demultiplexer_1_out3), .out4(demultiplexer_1_out4), .out5(demultiplexer_1_out5),
    .out6(demultiplexer_1_out6), .out7(demultiplexer_1_out7), .out8(demultiplexer_1_out8),
    .out9(demultiplexer_1_out9), .out10(demultiplexer_1_out10), .out11(demultiplexer_1_out11),
    .out12(demultiplexer_1_out12), .out13(demultiplexer_1_out13), .out14(demultiplexer_1_out14),
    .out15(demultiplexer_1_out15), .in(in_1), .sel(in_4));
  Reg16 reg16_1 (.out_4(reg16_1_out_4), .in_1(in_3), .in_2(demultiplexer_1_out0), .in_3(CLR));
  Reg16 reg16_2 (.out_4(reg16_2_out_4), .in_1(in_3), .in_2(demultiplexer_1_out1), .in_3(CLR));
  Reg16 reg16_3 (.out_4(reg16_3_out_4), .in_1(in_3), .in_2(demultiplexer_1_out2), .in_3(CLR));
  Reg16 reg16_4 (.out_4(reg16_4_out_4), .in_1(in_3), .in_2(demultiplexer_1_out3), .in_3(CLR));
  Reg16 reg16_5 (.out_4(reg16_5_out_4), .in_1(in_3), .in_2(demultiplexer_1_out4), .in_3(CLR));
  Reg16 reg16_6 (.out_4(reg16_6_out_4), .in_1(in_3), .in_2(demultiplexer_1_out5), .in_3(CLR));
  Reg16 reg16_7 (.out_4(reg16_7_out_4), .in_1(in_3), .in_2(demultiplexer_1_out6), .in_3(CLR));
  Reg16 reg16_8 (.out_4(reg16_8_out_4), .in_1(in_3), .in_2(demultiplexer_1_out7), .in_3(CLR));
  Reg16 reg16_9 (.out_4(reg16_9_out_4), .in_1(in_3), .in_2(demultiplexer_1_out8), .in_3(CLR));
  Reg16 reg16_10 (.out_4(reg16_10_out_4), .in_1(in_3), .in_2(demultiplexer_1_out9), .in_3(CLR));
  Reg16 reg16_11 (.out_4(reg16_11_out_4), .in_1(in_3), .in_2(demultiplexer_1_out10), .in_3(CLR));
  Reg16 reg16_12 (.out_4(reg16_12_out_4), .in_1(in_3), .in_2(demultiplexer_1_out11), .in_3(CLR));
  Reg16 reg16_13 (.out_4(reg16_13_out_4), .in_1(in_3), .in_2(demultiplexer_1_out12), .in_3(CLR));
  Reg16 reg16_14 (.out_4(reg16_14_out_4), .in_1(in_3), .in_2(demultiplexer_1_out13), .in_3(CLR));
  Reg16 reg16_15 (.out_4(reg16_15_out_4), .in_1(in_3), .in_2(demultiplexer_1_out14), .in_3(CLR));
  Reg16 reg16_16 (.out_4(reg16_16_out_4), .in_1(in_3), .in_2(demultiplexer_1_out15), .in_3(CLR));
  Multiplexer #(.enable("false"), .select(4), .width(16)) multiplexer_1 (
    .in0(reg16_1_out_4), .in1(reg16_2_out_4), .in2(reg16_3_out_4), .in3(reg16_4_out_4), .in4(reg16_5_out_4),
    .in5(reg16_6_out_4), .in6(reg16_7_out_4), .in7(reg16_8_out_4), .in8(reg16_9_out_4), .in9(reg16_10_out_4),
    .in10(reg16_11_out_4), .in11(reg16_12_out_4), .in12(reg16_13_out_4), .in13(reg16_14_out_4),
    .in14(reg16_15_out_4), .in15(reg16_16_out_4), .out(out_7), .sel(in_6));
  Multiplexer #(.enable("false"), .select(4), .width(16)) multiplexer_2 (
    .in0(reg16_1_out_4), .in1(reg16_2_out_4), .in2(reg16_3_out_4), .in3(reg16_4_out_4), .in4(reg16_5_out_4),
    .in5(reg16_6_out_4), .in6(reg16_7_out_4), .in7(reg16_8_out_4), .in8(reg16_9_out_4), .in9(reg16_10_out_4),
    .in10(reg16_11_out_4), .in11(reg16_12_out_4), .in12(reg16_13_out_4), .in13(reg16_14_out_4),
    .in14(reg16_15_out_4), .in15(reg16_16_out_4), .out(out_8), .sel(in_5));

  // Notes on the sheet:
  //   CLR: pull=down
endmodule

module Reg16TS (
  input  [15:0] in_1,
  input  in_2,
  input  in_3,
  output [15:0] out_4
);

  wire dipswitch_1_sw1, dipswitch_1_sw2, dipswitch_2_sw1, dipswitch_2_sw2, pull_resistor_5_node,
       pull_resistor_6_node, pull_resistor_8_node, pull_resistor_9_node, transistor_1_out, transistor_35_out,
       transistor_38_out, undriven;
  wire [15:0] pull_resistor_1_node, transistor_2_out;

  Pull_Resistor pull_resistor_1 (.node(pull_resistor_1_node));
  Register #(.width(16)) register_1 (.D(in_1), .Q(pull_resistor_1_node));  // open: en, clk, clr
  Transistor transistor_1 (.in(1'b1), .out(transistor_1_out), .gate(in_2));
  Transistor transistor_2 (.in(transistor_1_out), .out(transistor_2_out[0]), .gate(pull_resistor_1_node[0]));
  Transistor transistor_3 (.in(transistor_1_out), .out(transistor_2_out[1]), .gate(pull_resistor_1_node[1]));
  Transistor transistor_4 (.in(transistor_1_out), .out(transistor_2_out[2]), .gate(pull_resistor_1_node[2]));
  Transistor transistor_5 (.in(transistor_1_out), .out(transistor_2_out[3]), .gate(pull_resistor_1_node[3]));
  Transistor transistor_6 (.in(transistor_1_out), .out(transistor_2_out[4]), .gate(pull_resistor_1_node[4]));
  Transistor transistor_7 (.in(transistor_1_out), .out(transistor_2_out[5]), .gate(pull_resistor_1_node[5]));
  Transistor transistor_8 (.in(transistor_1_out), .out(transistor_2_out[6]), .gate(pull_resistor_1_node[6]));
  Transistor transistor_9 (.in(transistor_1_out), .out(transistor_2_out[7]), .gate(pull_resistor_1_node[7]));
  Transistor transistor_10 (.in(transistor_1_out), .out(transistor_2_out[8]), .gate(pull_resistor_1_node[8]));
  Transistor transistor_11 (.in(transistor_1_out), .out(transistor_2_out[9]), .gate(pull_resistor_1_node[9]));
  Transistor transistor_12 (.in(transistor_1_out), .out(transistor_2_out[10]), .gate(pull_resistor_1_node[10]));
  Transistor transistor_13 (.in(transistor_1_out), .out(transistor_2_out[11]), .gate(pull_resistor_1_node[11]));
  Transistor transistor_14 (.in(transistor_1_out), .out(transistor_2_out[12]), .gate(pull_resistor_1_node[12]));
  Transistor transistor_15 (.in(transistor_1_out), .out(transistor_2_out[13]), .gate(pull_resistor_1_node[13]));
  Transistor transistor_16 (.in(transistor_1_out), .out(transistor_2_out[14]), .gate(pull_resistor_1_node[14]));
  Transistor transistor_17 (.in(transistor_1_out), .out(transistor_2_out[15]), .gate(pull_resistor_1_node[15]));
  Pull_Resistor pull_resistor_2 (.node(transistor_1_out));
  Pull_Resistor pull_resistor_3 (.node(transistor_2_out));
  Transistor transistor_18 (.in(transistor_1_out), .out(out_4[0]), .gate(transistor_2_out[0]));
  Transistor transistor_19 (.in(transistor_1_out), .out(out_4[1]), .gate(transistor_2_out[1]));
  Transistor transistor_20 (.in(transistor_1_out), .out(out_4[2]), .gate(transistor_2_out[2]));
  Transistor transistor_21 (.in(transistor_1_out), .out(out_4[3]), .gate(transistor_2_out[3]));
  Transistor transistor_22 (.in(transistor_1_out), .out(out_4[4]), .gate(transistor_2_out[4]));
  Transistor transistor_23 (.in(transistor_1_out), .out(out_4[5]), .gate(transistor_2_out[5]));
  Transistor transistor_24 (.in(transistor_1_out), .out(out_4[6]), .gate(transistor_2_out[6]));
  Transistor transistor_25 (.in(transistor_1_out), .out(out_4[7]), .gate(transistor_2_out[7]));
  Transistor transistor_26 (.in(transistor_1_out), .out(out_4[8]), .gate(transistor_2_out[8]));
  Transistor transistor_27 (.in(transistor_1_out), .out(out_4[9]), .gate(transistor_2_out[9]));
  Transistor transistor_28 (.in(transistor_1_out), .out(out_4[10]), .gate(transistor_2_out[10]));
  Transistor transistor_29 (.in(transistor_1_out), .out(out_4[11]), .gate(transistor_2_out[11]));
  Transistor transistor_30 (.in(transistor_1_out), .out(out_4[12]), .gate(transistor_2_out[12]));
  Transistor transistor_31 (.in(transistor_1_out), .out(out_4[13]), .gate(transistor_2_out[13]));
  Transistor transistor_32 (.in(transistor_1_out), .out(out_4[14]), .gate(transistor_2_out[14]));
  Transistor transistor_33 (.in(transistor_1_out), .out(out_4[15]), .gate(transistor_2_out[15]));
  Pull_Resistor pull_resistor_4 (.node(out_4));
  Pull_Resistor #(.pull(1)) pull_resistor_5 (.node(pull_resistor_5_node));
  Transistor #(.\type ("n")) transistor_34 (.in(undriven), .out(pull_resistor_5_node), .gate(dipswitch_1_sw1));
  Transistor #(.\type ("n")) transistor_35 (.in(undriven), .out(transistor_35_out), .gate(dipswitch_1_sw2));
  DipSwitch dipswitch_1 (.sw1(dipswitch_1_sw1), .sw2(dipswitch_1_sw2));  // open: sw3, sw4, sw5, sw6, sw7, sw8
  Pull_Resistor pull_resistor_6 (.node(pull_resistor_6_node));
  Transistor transistor_36 (.in(1'b1), .out(pull_resistor_6_node), .gate(pull_resistor_5_node));
  Transistor transistor_37 (.in(1'b1), .out(pull_resistor_6_node), .gate(transistor_35_out));
  Transistor transistor_38 (.in(1'b1), .out(transistor_38_out), .gate(pull_resistor_6_node));
  Pull_Resistor pull_resistor_7 (.node(transistor_38_out));
  DipSwitch dipswitch_2 (.sw1(dipswitch_2_sw1), .sw2(dipswitch_2_sw2));  // open: sw3, sw4, sw5, sw6, sw7, sw8
  Pull_Resistor #(.pull(1)) pull_resistor_8 (.node(pull_resistor_8_node));
  Transistor #(.\type ("n")) transistor_39 (.in(1'b0), .out(pull_resistor_8_node), .gate(dipswitch_2_sw1));
  Transistor #(.\type ("n")) transistor_40 (.in(1'b0), .out(pull_resistor_8_node), .gate(dipswitch_2_sw2));
  Pull_Resistor #(.pull(1)) pull_resistor_9 (.node(pull_resistor_9_node));
  Transistor #(.\type ("n")) transistor_41 (.in(1'b0), .out(pull_resistor_9_node), .gate(pull_resistor_8_node));
endmodule

module Reg16 (
  input  [15:0] in_1,
  input  in_2,
  input  in_3,
  output [15:0] out_4
);

  Pull_Resistor pull_resistor_1 (.node(out_4));
  Register #(.width(16)) register_1 (.D(in_1), .en(in_2), .Q(out_4), .clk(in_2), .clr(in_3));
endmodule

module ALU (
  input  [4:0] OP,
  input  [15:0] B,
  input  [15:0] A,
  output [15:0] Q
);

  wire [15:0] adder_1_out, adder_2_out, adder_3_out, adder_4_out, adder_5_out, not_1_out, not_2_out,
       pull_resistor_1_node, undriven, undriven_2, undriven_3, undriven_4;

  assign not_1_out = ~A;  // NOT_Gate not_1, 16 bits wide
  Adder #(.width(16)) adder_1 (.a(not_1_out), .b({16{1'b0}}), .out(adder_1_out), .cin(1'b1));  // open: cout
  assign not_2_out = ~16'h1;  // NOT_Gate not_2, 16 bits wide
  Adder #(.width(16)) adder_2 (.a(A), .b(B), .out(adder_2_out));  // open: cin, cout
  Adder #(.width(16)) adder_3 (.a(A), .b(16'h1), .out(adder_3_out));  // open: cin, cout
  Adder #(.width(16)) adder_4 (.a(A), .b(adder_5_out), .out(adder_4_out));  // open: cin, cout
  Adder #(.width(16)) adder_5 (.a(not_2_out), .b({16{1'b0}}), .out(adder_5_out), .cin(1'b1));  // open: cout
  Pull_Resistor #(.pull("X")) pull_resistor_1 (.node(pull_resistor_1_node));
  Multiplexer #(.enable("false"), .select(5), .width(16)) multiplexer_1 (
    .in0({16{1'b0}}), .in1({16{1'b1}}), .in2(not_1_out), .in3(adder_1_out), .in4(undriven), .in5(undriven_3),
    .in6(undriven_2), .in8(undriven_4), .in10(adder_2_out), .in11(pull_resistor_1_node), .in14(adder_3_out),
    .in15(adder_4_out), .out(Q), .sel(OP));  // open: in7, in9, in12, in13, in16, in17, in18, in19, in20, in21, in22, in23, in24, in25, in26, in27, in28, in29, in30, in31

  // Notes on the sheet:
  //   A
  //   <B> (immediate)
  //   B
  //   Encoding
  //   n/a
  //   M: Alt bit
  //   XXXX XXXX XXXX XXXX
  //   <rB/rD> <rA> <ins> MZ10
  //   <rD> <rA> <ins> MZ11
  //   Z: 1 = Prevent changing ALU flags 
endmodule

module InstructionDecoder (
  input  [15:0] Instruction,
  output Long_Ins,
  output [1:0] Submodule
);

  wire bitfinder_1_found, transistor_1_out;
  wire [1:0] bitfinder_1_index;

  BitFinder #(.width(3)) bitfinder_1 (.in(Instruction[3:1]), .index(bitfinder_1_index), .found(bitfinder_1_found));
  Transistor #(.\type ("n")) transistor_1 (.in(1'b0), .out(transistor_1_out), .gate(bitfinder_1_found));
  Pull_Resistor #(.pull(1)) pull_resistor_1 (.node(transistor_1_out));
  Adder #(.width(2)) adder_1 (.a(bitfinder_1_index), .b(2'b00), .out(Submodule), .cin(transistor_1_out));  // open: cout

  assign Long_Ins = Instruction[0];
endmodule

module InstructionStore (
  input  LONG,
  input  [15:0] MEM,
  input  CLK,
  input  CLR,
  output [15:0] EX,
  output [15:0] O
);

  wire and_1_out, and_2_out, monostable_1_out_2, pull_resistor_1_node, pull_resistor_2_node,
       pull_resistor_3_node, pull_resistor_4_node, rslatch_1_out_3, transistor_6_out;

  Pull_Resistor #(.pull(1)) pull_resistor_1 (.node(pull_resistor_1_node));
  Transistor #(.\type ("n")) transistor_1 (.in(1'b0), .out(pull_resistor_1_node), .gate(CLK));
  Monostable monostable_1 (.out_2(monostable_1_out_2), .in_1(pull_resistor_1_node));
  Pull_Resistor #(.pull(1)) pull_resistor_2 (.node(pull_resistor_2_node));
  Transistor #(.\type ("n")) transistor_2 (.in(1'b0), .out(pull_resistor_2_node), .gate(1'b1));
  and and_1 (and_1_out, LONG, monostable_1_out_2);
  RSLatch rslatch_1 (.out_3(rslatch_1_out_3), .in_1(and_1_out), .in_2(and_2_out));  // open: out_4
  and and_2 (and_2_out, monostable_1_out_2, rslatch_1_out_3);
  Pull_Resistor #(.pull(1)) pull_resistor_3 (.node(pull_resistor_3_node));
  Transistor #(.\type ("n")) transistor_3 (.in(1'b0), .out(pull_resistor_3_node), .gate(rslatch_1_out_3));
  Pull_Resistor #(.pull(1)) pull_resistor_4 (.node(pull_resistor_4_node));
  Transistor #(.\type ("n")) transistor_4 (.in(1'b0), .out(pull_resistor_4_node), .gate(CLR));
  Transistor #(.\type ("n")) transistor_5 (.in(1'b0), .out(pull_resistor_4_node), .gate(pull_resistor_2_node));
  Pull_Resistor pull_resistor_5 (.node(LONG));
  Pull_Resistor pull_resistor_6 (.node(rslatch_1_out_3));
  Register #(.width(16)) register_1 (.D(MEM), .en(rslatch_1_out_3), .Q(EX), .clk(CLK), .clr(transistor_6_out));
  Register #(.width(16)) register_2 (.D(MEM), .en(pull_resistor_3_node), .Q(O), .clk(CLK), .clr(transistor_6_out));
  Transistor #(.\type ("n")) transistor_6 (.in(1'b0), .out(transistor_6_out), .gate(pull_resistor_4_node));
  Pull_Resistor #(.pull(1)) pull_resistor_7 (.node(transistor_6_out));

  // Notes on the sheet:
  //   Prevents Error State
endmodule

module EdgeDetector (
  input  I,
  output O
);

  wire monostable_1_out_2, monostable_2_out_2, pull_resistor_1_node;

  Pull_Resistor #(.pull(1)) pull_resistor_1 (.node(pull_resistor_1_node));
  Transistor #(.gate("br"), .\type ("n")) transistor_1 (.in(1'b0), .out(pull_resistor_1_node), .gate(I));
  Monostable monostable_1 (.out_2(monostable_1_out_2), .in_1(pull_resistor_1_node));
  Monostable monostable_2 (.out_2(monostable_2_out_2), .in_1(I));
  or or_1 (O, monostable_1_out_2, monostable_2_out_2);
endmodule

module ALUDecoder (
  input  [31:0] in_1,
  output FLG,
  output [4:0] OP,
  output [3:0] rA,
  output [3:0] rB,
  output bEN,
  output [3:0] rD,
  output [15:0] IME,
  output iEN
);

  wire [3:0] bit_extender_1_out;

  Bit_Extender #(.in_width(16), .out_width(4)) bit_extender_1 (.in(in_1[31:16]), .out(bit_extender_1_out));
  Pull_Resistor #(.pull(1)) pull_resistor_1 (.node(bEN));
  Transistor #(.\type ("n")) transistor_1 (.in(1'b0), .out(bEN), .gate(in_1[1]));
  Multiplexer #(.enable("false"), .width(4)) multiplexer_1 (
    .in0(bit_extender_1_out), .in1(in_1[15:12]), .out(rD), .sel(in_1[1]));

  assign FLG = in_1[2];
  assign iEN = in_1[1];
  assign IME = in_1[31:16];
  assign OP = {in_1[6:3], in_1[7]};
  assign rA = in_1[11:8];
  assign rB = in_1[15:12];

  // Notes on the sheet:
  //     <unspec:12>  <rD:4> <rB:4> <rA:4> <op:5> <flags:1>0X
  //   <ime:16>  <rD:4> <rA:4> <op:5> <flags:1>1X
endmodule

module CPUCore (
  input  CLK,
  input  ALUen,
  input  [15:0] DIn,
  input  [3:0] rD,
  input  IMEen,
  input  [3:0] rA,
  input  [3:0] rB,
  input  [4:0] ALUop,
  output [15:0] rAO,
  output [15:0] rBO
);

  wire demultiplexer_1_out0, demultiplexer_1_out1, demultiplexer_1_out2, demultiplexer_1_out3,
       demultiplexer_1_out4, demultiplexer_1_out5, demultiplexer_1_out6, demultiplexer_1_out7,
       demultiplexer_1_out8, demultiplexer_1_out9, demultiplexer_1_out10, demultiplexer_1_out11,
       demultiplexer_1_out12, demultiplexer_1_out13, demultiplexer_1_out14, demultiplexer_1_out15, por_1_out;
  wire [15:0] alu_1_q, multiplexer_1_out, multiplexer_2_out, r4multibus_1_out_12, r4multibus_1_out_13,
       reg16_1_out_4, reg16_2_out_4, reg16_3_out_4, reg16_4_out_4, reg16_5_out_4, reg16_6_out_4,
       reg16_7_out_4, reg16_8_out_4, reg16_9_out_4, reg16_10_out_4, reg16_11_out_4, reg16_12_out_4,
       reg16_13_out_4, reg16_14_out_4, reg16_15_out_4, reg16_16_out_4;

  Demultiplexer #(.enable("false"), .select(4)) demultiplexer_1 (
    .out0(demultiplexer_1_out0), .out1(demultiplexer_1_out1), .out2(demultiplexer_1_out2),
    .out3(demultiplexer_1_out3), .out4(demultiplexer_1_out4), .out5(demultiplexer_1_out5),
    .out6(demultiplexer_1_out6), .out7(demultiplexer_1_out7), .out8(demultiplexer_1_out8),
    .out9(demultiplexer_1_out9), .out10(demultiplexer_1_out10), .out11(demultiplexer_1_out11),
    .out12(demultiplexer_1_out12), .out13(demultiplexer_1_out13), .out14(demultiplexer_1_out14),
    .out15(demultiplexer_1_out15), .in(CLK), .sel(rD));
  // Probe on rD
  POR por_1 (.out(por_1_out));
  Multiplexer #(.enable("false"), .width(16)) multiplexer_1 (
    .in0(DIn), .in1(alu_1_q), .out(multiplexer_1_out), .sel(ALUen));
  Reg16 reg16_1 (.out_4(reg16_1_out_4), .in_1(multiplexer_1_out), .in_2(demultiplexer_1_out0), .in_3(por_1_out));
  Reg16 reg16_2 (.out_4(reg16_2_out_4), .in_1(multiplexer_1_out), .in_2(demultiplexer_1_out1), .in_3(por_1_out));
  Reg16 reg16_3 (.out_4(reg16_3_out_4), .in_1(multiplexer_1_out), .in_2(demultiplexer_1_out2), .in_3(por_1_out));
  Reg16 reg16_4 (.out_4(reg16_4_out_4), .in_1(multiplexer_1_out), .in_2(demultiplexer_1_out3), .in_3(por_1_out));
  R4MultiBus r4multibus_1 (
    .out_13(r4multibus_1_out_13), .out_10(rAO), .out_11(rBO), .out_12(r4multibus_1_out_12),
    .in_5(reg16_4_out_4), .in_6(reg16_3_out_4), .in_7(reg16_2_out_4), .in_8(reg16_1_out_4), .in_9(2'b00),
    .in_1(rA), .in_2(rB), .in_3(4'b0000), .in_4(4'b0000));
  Multiplexer #(.enable("false"), .width(16)) multiplexer_2 (
    .in0(rBO), .in1(DIn), .out(multiplexer_2_out), .sel(IMEen));
  ALU alu_1 (.Q(alu_1_q), .OP(ALUop), .B(multiplexer_2_out), .A(rAO));
  Reg16 reg16_5 (.out_4(reg16_5_out_4), .in_1(multiplexer_1_out), .in_2(demultiplexer_1_out4), .in_3(por_1_out));
  Reg16 reg16_6 (.out_4(reg16_6_out_4), .in_1(multiplexer_1_out), .in_2(demultiplexer_1_out5), .in_3(por_1_out));
  Reg16 reg16_7 (.out_4(reg16_7_out_4), .in_1(multiplexer_1_out), .in_2(demultiplexer_1_out6), .in_3(por_1_out));
  Reg16 reg16_8 (.out_4(reg16_8_out_4), .in_1(multiplexer_1_out), .in_2(demultiplexer_1_out7), .in_3(por_1_out));
  R4MultiBus r4multibus_2 (
    .out_13(r4multibus_1_out_13), .out_10(rAO), .out_11(rBO), .out_12(r4multibus_1_out_12),
    .in_5(reg16_8_out_4), .in_6(reg16_7_out_4), .in_7(reg16_6_out_4), .in_8(reg16_5_out_4), .in_9(2'b01),
    .in_1(rA), .in_2(rB), .in_3(4'b0000), .in_4(4'b0000));
  // Probe on alu_1_q
  Reg16 reg16_9 (.out_4(reg16_9_out_4), .in_1(multiplexer_1_out), .in_2(demultiplexer_1_out8), .in_3(por_1_out));
  Reg16 reg16_10 (.out_4(reg16_10_out_4), .in_1(multiplexer_1_out), .in_2(demultiplexer_1_out9), .in_3(por_1_out));
  Reg16 reg16_11 (.out_4(reg16_11_out_4), .in_1(multiplexer_1_out), .in_2(demultiplexer_1_out10), .in_3(por_1_out));
  Reg16 reg16_12 (.out_4(reg16_12_out_4), .in_1(multiplexer_1_out), .in_2(demultiplexer_1_out11), .in_3(por_1_out));
  R4MultiBus r4multibus_3 (
    .out_13(r4multibus_1_out_13), .out_10(rAO), .out_11(rBO), .out_12(r4multibus_1_out_12),
    .in_5(reg16_12_out_4), .in_6(reg16_11_out_4), .in_7(reg16_10_out_4), .in_8(reg16_9_out_4), .in_9(2'b10),
    .in_1(rA), .in_2(rB), .in_3(4'b0000), .in_4(4'b0000));
  Reg16 reg16_13 (.out_4(reg16_13_out_4), .in_1(multiplexer_1_out), .in_2(demultiplexer_1_out12), .in_3(por_1_out));
  Reg16 reg16_14 (.out_4(reg16_14_out_4), .in_1(multiplexer_1_out), .in_2(demultiplexer_1_out13), .in_3(por_1_out));
  Reg16 reg16_15 (.out_4(reg16_15_out_4), .in_1(multiplexer_1_out), .in_2(demultiplexer_1_out14), .in_3(por_1_out));
  Reg16 reg16_16 (.out_4(reg16_16_out_4), .in_1(multiplexer_1_out), .in_2(demultiplexer_1_out15), .in_3(por_1_out));
  R4MultiBus r4multibus_4 (
    .out_13(r4multibus_1_out_13), .out_10(rAO), .out_11(rBO), .out_12(r4multibus_1_out_12),
    .in_5(reg16_16_out_4), .in_6(reg16_15_out_4), .in_7(reg16_14_out_4), .in_8(reg16_13_out_4), .in_9(2'b11),
    .in_1(rA), .in_2(rB), .in_3(4'b0000), .in_4(4'b0000));
  // Probe on rA
  // Probe on rAO
  // Probe on rB
  // Probe on rBO
  // Probe on 4'b0000
  // Probe on r4multibus_1_out_12
  // Probe on 4'b0000
  // Probe on r4multibus_1_out_13
endmodule

module R4BusController (
  input  [15:0] in_1,
  input  [15:0] in_2,
  input  [15:0] in_3,
  input  [15:0] in_4,
  input  [3:0] in_5,
  input  [1:0] Group,
  output [15:0] BOut
);

  wire and_1_out;
  wire [1:0] xnor_1_out;

  assign xnor_1_out = ~(in_5[3:2] ^ Group);  // XNOR_Gate xnor_1, 2 bits wide
  and and_1 (and_1_out, xnor_1_out[0], xnor_1_out[1]);
  Multiplexer #(.disabled("Z"), .select(2), .width(16)) multiplexer_1 (
    .in0(in_1), .in1(in_2), .in2(in_3), .in3(in_4), .out(BOut), .sel(in_5[1:0]), .en(and_1_out));

  // Notes on the sheet:
  //   Addr
endmodule

module R4MultiBus (
  input  [3:0] in_1,
  input  [3:0] in_2,
  input  [3:0] in_3,
  input  [3:0] in_4,
  input  [15:0] in_5,
  input  [15:0] in_6,
  input  [15:0] in_7,
  input  [15:0] in_8,
  input  [1:0] in_9,
  output [15:0] out_10,
  output [15:0] out_11,
  output [15:0] out_12,
  output [15:0] out_13
);

  R4BusController r4buscontroller_1 (
    .BOut(out_10), .in_5(in_1), .Group(in_9), .in_1(in_8), .in_2(in_7), .in_3(in_6), .in_4(in_5));
  R4BusController r4buscontroller_2 (
    .BOut(out_11), .in_5(in_2), .Group(in_9), .in_1(in_8), .in_2(in_7), .in_3(in_6), .in_4(in_5));
  R4BusController r4buscontroller_3 (
    .BOut(out_12), .in_5(in_3), .Group(in_9), .in_1(in_8), .in_2(in_7), .in_3(in_6), .in_4(in_5));
  R4BusController r4buscontroller_4 (
    .BOut(out_13), .in_5(in_4), .Group(in_9), .in_1(in_8), .in_2(in_7), .in_3(in_6), .in_4(in_5));
endmodule
